# Fritzing sketch HitSensor (saved by Fritzing 0.9.3b)
breadboards: 1

parts:
  R1 = PHOTOCELL [package=photocell]
  R2 = Resistor [tolerance=±5% resistance=2k package="0402 [SMD]"]

nets:
  N1: R1.P$2, R2.Pin_0
