# Fritzing sketch PhaserInternals (saved by Fritzing 0.9.3b)
breadboards: 1

parts:
  Part1 = Arduino Uno (Rev3)
  J1 = Piezo Speaker
  R1 = Resistor [tolerance=±5% resistance=100 package="0603 [SMD]"]
  S1 = Momentary Switch [package=ksa_sealed_tac_switch]
  R2 = Resistor [tolerance=±5% resistance=220 package="0603 [SMD]"]
  LED1 = Super Flux LED blue [color=Blue]
  U1 = 74HC595 [package="DIP16 [THT]"]
  R3 = Resistor [tolerance=±5% resistance=220 package="0805 [SMD]"]
  J2 = Piezo Speaker

nets:
  N1: Part1.D9_PWM, J1.pin2, J2.pin2
  N2: Part1.D2, U1.DS
  N3: Part1.D3_PWM, U1.ST_CP
  N4: Part1.D4, U1.SH_CP
  N5: Part1.D5_PWM, S1.1
  GND: Part1.D6_PWM, Part1.GND, R1.Pin_0, R2.Pin_1, LED1.cathode, U1.GND, U1.OE, R3.Pin_0
  5V: Part1.5V, S1.3, U1.MR, U1.VCC
  N6: J1.pin1, R1.Pin_1, J2.pin1
  N7: S1.2, R2.Pin_0
